# Fritzing sketch schematics (saved by Fritzing 0.9.9b)
breadboards: 1

parts:
  Display1 = LCD screen 16x2 IIC [part_number=101290]
  Part2 = Arduino Mega ADK (Rev3)
  PIR1 = PIR sensor
  HC-SR04_Sensor_1 = HC-SR04 Ultrasonic Distance Sensor
  RHT1 = Humidity and Temperature Sensor RHT03
  U2 = GAS_SENSOR [package=mq-3]
  Part3 = Soil Moisture Sensor
  J2 = Basic Servo
  J1 = Piezo Speaker
  WeMos_D1_Mini_Relay_Shield1 = WeMos D1 Mini Relay Shield

nets:
  GND: Display1.GND, PIR1.GND, HC-SR04_Sensor_1.GND, RHT1.GND_1, RHT1.GND_2, U2.A1, Part3.GND, J2.gnd, J1.pin1, WeMos_D1_Mini_Relay_Shield1.G
  VCC: Display1.VCC, PIR1.VDD, HC-SR04_Sensor_1.VCC, RHT1.Vcc, U2.B1, Part3.VCC, J2.vcc, WeMos_D1_Mini_Relay_Shield1.5V
  N1: Display1.SDA, Part2.D20/SDA
  N2: Display1.SCL, Part2.D21/SCL
  N3: Part2.A0, Part3.SIG
  N4: Part2.D13_PWM, J1.pin2
  N5: Part2.D12_PWM, HC-SR04_Sensor_1.TRIG
  N6: Part2.D11_PWM, HC-SR04_Sensor_1.ECHO
  N7: Part2.D5_PWM, J2.pulse
  N8: Part2.D7_PWM, U2.H1
  N9: Part2.D47, PIR1.SIG
  N10: Part2.D49, RHT1.Data-signal

custom parts:
  LCD screen 16x2 IIC: LCD screen with HD44780 controller enables showing text, symbols, value or anything else that comes from Croduino/Arduino. It is capable of showing 16 symbols in two lines and therefore can be used in many projects that need to send clearly visible and legible output information.. • Color of symbols: White • Backlight: Blue • Dimensions: 80 x 36 x 12 mm • Screen dimensions: 64.5 x 16 mm •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
